// Digital circuit Projet1.dig as structural Verilog
module Projet1 (
  input  C,
  input  B,
  input  A,
  output Out
);

  wire nand_1_out, nand_2_out, nand_3_out, not_1_out, not_2_out, not_3_out, not_4_out;

  not not_1 (not_1_out, C);
  not not_2 (not_2_out, B);
  not not_3 (not_3_out, A);
  not not_4 (not_4_out, A);
  nand nand_1 (nand_1_out, not_1_out, not_2_out, not_3_out);
  nand nand_2 (nand_2_out, C, B, not_4_out);
  nand nand_3 (nand_3_out, C, B, A);
  nand nand_4 (Out, nand_1_out, nand_2_out, nand_3_out);
endmodule
