// Digital circuit Projet1_v2.dig as structural Verilog
module Projet1_v2 (
  input  C,
  input  B,
  input  A,
  output Out
);

  wire nand_1_out, nand_2_out, not_1_out, not_2_out, not_3_out;

  not not_1 (not_1_out, C);
  not not_2 (not_2_out, B);
  not not_3 (not_3_out, A);
  nand nand_1 (nand_1_out, C, B);
  nand nand_2 (nand_2_out, not_1_out, not_2_out, not_3_out);
  nand nand_3 (Out, nand_1_out, nand_2_out);
endmodule
