// Digital circuit Projet2.dig as structural Verilog
module Projet2 (
  input  D,
  input  C,
  input  B,
  input  A,
  output F
);

  wire and_1_out, and_2_out, not_1_out, not_2_out, not_3_out, not_4_out;

  not not_1 (not_1_out, B);
  not not_2 (not_2_out, A);
  not not_3 (not_3_out, D);
  not not_4 (not_4_out, A);
  and and_1 (and_1_out, D, C, not_1_out, not_2_out);
  and and_2 (and_2_out, not_3_out, C, B, not_4_out);
  or or_1 (F, and_1_out, and_2_out);
endmodule
