// Digital circuit 2BitsAdder.dig as structural Verilog
module _2BitsAdder (
  input  A0,
  input  A1,
  input  B0,
  input  B1,
  output S0,
  output C0,
  output S1,
  output C1
);

  wire and_2_out, and_3_out, xor_2_out;

  xor xor_1 (S0, B0, A0);
  and and_1 (C0, A0, B0);
  xor xor_2 (xor_2_out, B1, A1);
  and and_2 (and_2_out, A1, B1);
  xor xor_3 (S1, C0, xor_2_out);
  and and_3 (and_3_out, xor_2_out, C0);
  or or_1 (C1, and_3_out, and_2_out);
endmodule
