// Digital circuit 2BitsAdder_v2.dig as structural Verilog
module _2BitsAdder_v2 (
  input  A1,
  input  A0,
  input  B1,
  input  B0,
  output C0,
  output C1,
  output S1,
  output S0
);

  half_adder half_adder_1 (.A(A0), .B(B0), .Y(S0), .C(C0));
  full_adder full_adder_1 (.A(A1), .B(B1), .Ci(C0), .Y(S1), .Co(C1));
endmodule
