// Digital circuit full_adder.dig as structural Verilog
module full_adder (
  input  A,
  input  B,
  input  Ci,
  output Y,
  output Co
);

  wire half_adder_1_c, half_adder_1_y, half_adder_2_c;

  half_adder half_adder_1 (.A(A), .B(B), .Y(half_adder_1_y), .C(half_adder_1_c));
  half_adder half_adder_2 (.A(Ci), .B(half_adder_1_y), .Y(Y), .C(half_adder_2_c));
  or or_1 (Co, half_adder_2_c, half_adder_1_c);
endmodule
