// Digital circuit 3BitsAdder.dig as structural Verilog
module _3BitsAdder (
  input  A0,
  input  A1,
  input  B0,
  input  B1,
  input  A2,
  input  B2,
  output S0,
  output S1,
  output S2,
  output C2
);

  wire and_1_out, and_2_out, and_3_out, and_4_out, and_5_out, or_1_out, xor_2_out, xor_3_out;

  xor xor_1 (S0, B0, A0);
  and and_1 (and_1_out, A0, B0);
  xor xor_2 (xor_2_out, B1, A1);
  and and_2 (and_2_out, A1, B1);
  xor xor_3 (xor_3_out, B2, A2);
  and and_3 (and_3_out, A2, B2);
  xor xor_4 (S1, and_1_out, xor_2_out);
  and and_4 (and_4_out, xor_2_out, and_1_out);
  or or_1 (or_1_out, and_4_out, and_2_out);
  xor xor_5 (S2, or_1_out, xor_3_out);
  and and_5 (and_5_out, xor_3_out, or_1_out);
  or or_2 (C2, and_5_out, and_3_out);
endmodule
