// Digital circuit 3BitsAdder_circuit.dig as structural Verilog
module _3BitsAdder_circuit (
  input  A2,
  input  A1,
  input  A0,
  input  B2,
  input  B1,
  input  B0,
  output Y3,
  output Y2,
  output Y1,
  output Y0
);

  wire _7408_1_pin3, _7408_1_pin6, _7408_1_pin8, _7408_1_pin11, _7486_1_pin2, _7486_1_pin8, C0, C1;

  _7486 _7486_1 (
    .pin1(C1), .pin2(_7486_1_pin2), .pin3(Y2), .pin4(B2), .pin5(A2), .pin6(_7486_1_pin2), .pin7(1'b0),
    .pin8(_7486_1_pin8), .pin9(A1), .pin10(B1), .pin11(Y1), .pin12(_7486_1_pin8), .pin13(C0), .pin14(1'b1));
  _7408 _7408_1 (
    .pin1(_7486_1_pin2), .pin2(C1), .pin3(_7408_1_pin3), .pin4(B2), .pin5(A2), .pin6(_7408_1_pin6),
    .pin7(1'b0), .pin8(_7408_1_pin8), .pin9(A1), .pin10(B1), .pin11(_7408_1_pin11), .pin12(C0),
    .pin13(_7486_1_pin8), .pin14(1'b1));
  _7432 _7432_1 (
    .pin1(_7408_1_pin6), .pin2(_7408_1_pin3), .pin3(Y3), .pin4(1'b1), .pin5(1'b1), .pin7(1'b0), .pin9(1'b1),
    .pin10(1'b1), .pin11(C1), .pin12(_7408_1_pin11), .pin13(_7408_1_pin8), .pin14(1'b1));  // open: pin6, pin8
  _7486 _7486_2 (
    .pin1(1'b1), .pin2(1'b1), .pin4(1'b1), .pin5(1'b1), .pin7(1'b0), .pin9(1'b1), .pin10(1'b1), .pin11(Y0),
    .pin12(A0), .pin13(B0), .pin14(1'b1));  // open: pin3, pin6, pin8
  _7408 _7408_2 (
    .pin1(1'b1), .pin2(1'b1), .pin4(1'b1), .pin5(1'b1), .pin7(1'b0), .pin9(1'b1), .pin10(1'b1), .pin11(C0),
    .pin12(A0), .pin13(B0), .pin14(1'b1));  // open: pin3, pin6, pin8

  // Other names for the same wires on the sheet: C2 = Y3; S0 = Y0; S1 = Y1; S2 = Y2
endmodule
