// Digital circuit 3BitsAdder_v2.dig as structural Verilog
module _3BitsAdder_v2 (
  input  A1,
  input  A0,
  input  B1,
  input  B0,
  input  A2,
  input  B2,
  output S1,
  output S0,
  output C2,
  output S2
);

  wire fulladder_1_p5, halfadder_1_p4;

  // HalfAdder halfadder_1: pin names not known; wires that end beside it: A0, B0, S0, halfadder_1_p4
  // FullAdder fulladder_1: pin names not known; wires that end beside it: A1, B1, halfadder_1_p4, S1, fulladder_1_p5
  // FullAdder fulladder_2: pin names not known; wires that end beside it: A2, B2, fulladder_1_p5, S2, C2
endmodule
