// Digital circuit cSegment.dig as structural Verilog
module cSegment (
  input  N3,
  input  N2,
  input  N1,
  input  N0,
  output Y
);

  Multiplexer #(.Selector_Bits(3)) multiplexer_1 (
    .sel({N3, N2, N1}), .in_0(1'b1), .in_1(N0), .in_2(1'b1), .in_3(1'b1), .in_4(1'b1), .in_5(1'b1),
    .in_6(N0), .in_7(1'b0), .out(Y));
endmodule
