// Digital circuit full_lab.dig as structural Verilog
module full_lab (
  input  A2,
  input  A1,
  input  A0,
  input  B2,
  input  B1,
  input  B0,
  output Y3,
  output Y2,
  output Y1,
  output Y0
);

  wire _7408_1_pin3, _7408_1_pin6, _7408_1_pin8, _7408_1_pin11, _7486_1_pin2, _7486_1_pin8, C, C0, C1,
       segments_1_a, segments_1_b, segments_1_d, segments_1_e, segments_1_f, segments_1_g;

  _7486 _7486_1 (
    .pin1(C1), .pin2(_7486_1_pin2), .pin3(Y2), .pin4(B2), .pin5(A2), .pin6(_7486_1_pin2), .pin7(1'b0),
    .pin8(_7486_1_pin8), .pin9(A1), .pin10(B1), .pin11(Y1), .pin12(_7486_1_pin8), .pin13(C0), .pin14(1'b1));
  _7408 _7408_1 (
    .pin1(_7486_1_pin2), .pin2(C1), .pin3(_7408_1_pin3), .pin4(B2), .pin5(A2), .pin6(_7408_1_pin6),
    .pin7(1'b0), .pin8(_7408_1_pin8), .pin9(A1), .pin10(B1), .pin11(_7408_1_pin11), .pin12(C0),
    .pin13(_7486_1_pin8), .pin14(1'b1));
  _7432 _7432_1 (
    .pin1(_7408_1_pin6), .pin2(_7408_1_pin3), .pin3(Y3), .pin4(1'b1), .pin5(1'b1), .pin7(1'b0), .pin9(1'b1),
    .pin10(1'b1), .pin11(C1), .pin12(_7408_1_pin11), .pin13(_7408_1_pin8), .pin14(1'b1));  // open: pin6, pin8
  segments segments_1 (
    .N3(Y3), .N2(Y2), .N1(Y1), .N0(Y0), .A(segments_1_a), .B(segments_1_b), .D(segments_1_d),
    .E(segments_1_e), .F(segments_1_f), .G(segments_1_g));  // open: C
  Seven_Seg seven_seg_1 (
    .a(segments_1_a), .b(segments_1_b), .c(C), .d(segments_1_d), .e(segments_1_e), .f(segments_1_f),
    .g(segments_1_g), .dp(1'b0));
  _7486 _7486_2 (
    .pin1(1'b1), .pin2(1'b1), .pin4(1'b1), .pin5(1'b1), .pin7(1'b0), .pin9(1'b1), .pin10(1'b1), .pin11(Y0),
    .pin12(A0), .pin13(B0), .pin14(1'b1));  // open: pin3, pin6, pin8
  _74151 _74151_1 (
    .pin1(1'b1), .pin2(1'b1), .pin3(Y0), .pin4(1'b1), .pin5(C), .pin7(1'b0), .pin8(1'b0), .pin9(Y3),
    .pin10(Y2), .pin11(Y1), .pin12(1'b0), .pin13(Y0), .pin14(1'b1), .pin15(1'b1), .pin16(1'b1));  // open: pin6
  _7408 _7408_2 (
    .pin1(1'b1), .pin2(1'b1), .pin4(1'b1), .pin5(1'b1), .pin7(1'b0), .pin9(1'b1), .pin10(1'b1), .pin11(C0),
    .pin12(A0), .pin13(B0), .pin14(1'b1));  // open: pin3, pin6, pin8

  // Other names for the same wires on the sheet: C2 = Y3; S0 = Y0; S1 = Y1; S2 = Y2
endmodule
