// Digital circuit segments.dig as structural Verilog
module segments (
  input  N3,
  input  N2,
  input  N1,
  input  N0,
  output A,
  output B,
  output C,
  output D,
  output E,
  output F,
  output G
);

  wire _74151_1_pin4, _74151_2_pin2, _74151_4_pin2, _74151_5_pin4, _74151_6_pin1, _74151_6_pin4,
       _74151_7_pin1;

  _74151 _74151_1 (
    .pin1(1'b1), .pin2(N0), .pin3(1'b1), .pin4(_74151_1_pin4), .pin5(A), .pin7(1'b0), .pin8(1'b0), .pin9(N3),
    .pin10(N2), .pin11(N1), .pin12(1'b1), .pin13(1'b1), .pin14(1'b1), .pin15(1'b1), .pin16(1'b1));  // open: pin6
  not not_1 (_74151_1_pin4, N0);
  _74151 _74151_2 (
    .pin1(N0), .pin2(_74151_2_pin2), .pin3(1'b1), .pin4(1'b1), .pin5(B), .pin7(1'b0), .pin8(1'b0), .pin9(N3),
    .pin10(N2), .pin11(N1), .pin12(1'b0), .pin13(N0), .pin14(1'b1), .pin15(1'b1), .pin16(1'b1));  // open: pin6
  not not_2 (_74151_2_pin2, N0);
  _74151 _74151_3 (
    .pin1(1'b1), .pin2(1'b1), .pin3(N0), .pin4(1'b1), .pin5(C), .pin7(1'b0), .pin8(1'b0), .pin9(N3),
    .pin10(N2), .pin11(N1), .pin12(1'b0), .pin13(N0), .pin14(1'b1), .pin15(1'b1), .pin16(1'b1));  // open: pin6
  Seven_Seg seven_seg_1 (.a(A), .b(B), .c(C), .d(D), .e(E), .f(F), .g(G), .dp(1'b0));
  _74151 _74151_4 (
    .pin1(1'b1), .pin2(_74151_4_pin2), .pin3(N3), .pin4(1'b1), .pin5(D), .pin7(1'b0), .pin8(1'b0), .pin9(N2),
    .pin10(N1), .pin11(N0), .pin12(1'b0), .pin13(1'b1), .pin14(1'b1), .pin15(N3), .pin16(1'b1));  // open: pin6
  not not_3 (_74151_4_pin2, N3);
  _74151 _74151_5 (
    .pin1(1'b0), .pin2(1'b1), .pin3(1'b0), .pin4(_74151_5_pin4), .pin5(E), .pin7(1'b0), .pin8(1'b0),
    .pin9(N3), .pin10(N1), .pin11(N0), .pin12(1'b1), .pin13(1'b1), .pin14(N2), .pin15(1'b1), .pin16(1'b1));  // open: pin6
  not not_4 (_74151_5_pin4, N2);
  _74151 _74151_6 (
    .pin1(_74151_6_pin1), .pin2(1'b1), .pin3(1'b0), .pin4(_74151_6_pin4), .pin5(F), .pin7(1'b0), .pin8(1'b0),
    .pin9(N3), .pin10(N2), .pin11(N1), .pin12(1'b1), .pin13(1'b1), .pin14(1'b1), .pin15(1'b1), .pin16(1'b1));  // open: pin6
  not not_5 (_74151_6_pin1, N0);
  not not_6 (_74151_6_pin4, N0);
  _74151 _74151_7 (
    .pin1(_74151_7_pin1), .pin2(1'b1), .pin3(1'b1), .pin4(1'b0), .pin5(G), .pin7(1'b0), .pin8(1'b0),
    .pin9(N3), .pin10(N2), .pin11(N1), .pin12(1'b1), .pin13(1'b0), .pin14(1'b1), .pin15(1'b1), .pin16(1'b1));  // open: pin6
  not not_7 (_74151_7_pin1, N0);
endmodule
