// Digital circuit demux.dig as structural Verilog
module demux (
  input  D,
  input  C,
  input  B,
  input  A,
  output S
);

  wire and_1_out, and_2_out, and_3_out, demultiplexer_1_out_0, demultiplexer_1_out_1, demultiplexer_1_out_2,
       demultiplexer_1_out_3, demultiplexer_1_out_4, demultiplexer_1_out_5, demultiplexer_1_out_6,
       demultiplexer_1_out_7, not_1_out;

  Demultiplexer #(.Selector_Bits(3)) demultiplexer_1 (
    .sel({C, B, A}), .in(1'b1), .out_0(demultiplexer_1_out_0), .out_1(demultiplexer_1_out_1),
    .out_2(demultiplexer_1_out_2), .out_3(demultiplexer_1_out_3), .out_4(demultiplexer_1_out_4),
    .out_5(demultiplexer_1_out_5), .out_6(demultiplexer_1_out_6), .out_7(demultiplexer_1_out_7));
  and and_1 (and_1_out, demultiplexer_1_out_2, D);
  and and_2 (and_2_out, D, demultiplexer_1_out_3);
  and and_3 (and_3_out, demultiplexer_1_out_7, not_1_out);
  not not_1 (not_1_out, D);
  or or_1 (S, demultiplexer_1_out_1, and_1_out, and_2_out, demultiplexer_1_out_5, demultiplexer_1_out_6, and_3_out);
endmodule
