// Digital circuit demux_circuit.dig as structural Verilog
module demux_circuit (
  input  N3,
  input  N2,
  input  N1,
  input  N0,
  output S
);

  wire _7404_1_p2, _7408_1_pin3, _7408_1_pin8, _7408_1_pin11, _7432_1_pin8, _7432_1_pin10, _7432_2_pin5,
       _7432_2_pin10, _74238_1_pin7, _74238_1_pin9, _74238_1_pin10, _74238_1_pin12, _74238_1_pin13,
       _74238_1_pin14;

  _74238 _74238_1 (
    .pin1(N0), .pin2(N1), .pin3(N2), .pin4(1'b0), .pin5(1'b0), .pin6(1'b1), .pin7(_74238_1_pin7),
    .pin8(1'b0), .pin9(_74238_1_pin9), .pin10(_74238_1_pin10), .pin12(_74238_1_pin12),
    .pin13(_74238_1_pin13), .pin14(_74238_1_pin14), .pin16(1'b1));  // open: pin11, pin15
  // _7404 _7404_1: pin names not known; wires that end beside it: N3, _7404_1_p2, 1'b0
  _7408 _7408_1 (
    .pin1(_74238_1_pin7), .pin2(_7404_1_p2), .pin3(_7408_1_pin3), .pin8(_7408_1_pin8), .pin9(N3),
    .pin10(_74238_1_pin13), .pin11(_7408_1_pin11), .pin12(N3), .pin13(_74238_1_pin12), .pin14(1'b1));  // open: pin4, pin5, pin6, pin7
  _7432 _7432_1 (
    .pin8(_7432_1_pin8), .pin9(_74238_1_pin14), .pin10(_7432_1_pin10), .pin11(_7432_1_pin10),
    .pin12(_7408_1_pin11), .pin13(_7408_1_pin8), .pin14(1'b1));  // open: pin1, pin2, pin3, pin4, pin5, pin6, pin7
  _7432 _7432_2 (
    .pin4(_7408_1_pin3), .pin5(_7432_2_pin5), .pin6(S), .pin7(1'b0), .pin8(_7432_2_pin5),
    .pin9(_7432_1_pin8), .pin10(_7432_2_pin10), .pin11(_7432_2_pin10), .pin12(_74238_1_pin10),
    .pin13(_74238_1_pin9), .pin14(1'b1));  // open: pin1, pin2, pin3
endmodule
