// Digital circuit Lab5.dig as structural Verilog
module Lab5 (
  input  clk,
  input  D,
  input  T,
  input  J,
  input  K,
  output D_out,
  output T_out,
  output JK_out
);

  D_FF d_ff_1 (.D(D), .C(clk), .Q(D_out));  // open: nQ
  T_FF t_ff_1 (.T(T), .C(clk), .Q(T_out));  // open: nQ
  JK_FF jk_ff_1 (.J(J), .C(clk), .K(K), .Q(JK_out));  // open: nQ
endmodule
