// Digital circuit Labo6.dig as structural Verilog
module Labo6 (
  input  clk,
  output out_2,
  output out_3,
  output out_4,
  output out_5
);

  wire _74164_1_pin1;

  _74164 _74164_1 (
    .pin1(_74164_1_pin1), .pin2(_74164_1_pin1), .pin3(out_2), .pin4(out_3), .pin5(out_4), .pin6(out_5),
    .pin7(1'b0), .pin8(clk), .pin9(1'b1), .pin14(1'b1));  // open: pin10, pin11, pin12, pin13
  _7410 _7410_1 (
    .pin1(1'b1), .pin2(1'b1), .pin3(out_4), .pin4(out_3), .pin5(out_2), .pin6(_74164_1_pin1), .pin7(1'b0),
    .pin9(1'b1), .pin10(1'b1), .pin11(1'b1), .pin13(1'b1), .pin14(1'b1));  // open: pin8, pin12
endmodule
