// Digital circuit projet1.dig as structural Verilog
module projet1 (
  input  clk
);

  wire and_1_out, nQ0, Q1, Q2;
  wire [0:0] jk_ff_3_q;

  and and_1 (and_1_out, nQ0, Q2);
  JK_FF jk_ff_1 (.J(nQ0), .C(clk), .K(1'b1), .Q(Q2));  // open: nQ
  JK_FF jk_ff_2 (.J(1'b1), .C(clk), .K(and_1_out), .Q(Q1));  // open: nQ
  JK_FF jk_ff_3 (.J(Q2), .C(clk), .K(Q1), .Q(jk_ff_3_q[0]), .nQ(nQ0));
  LED led_1 (.in(clk));
  Seven_Seg_Hex seven_seg_hex_1 (.d({3'b000, Q1}), .dp(1'b0));
  Seven_Seg_Hex seven_seg_hex_2 (.d({3'b000, jk_ff_3_q[0]}), .dp(1'b0));
endmodule
