// Digital circuit projet2.dig as structural Verilog
module projet2 (
  input  clk,
  input  A
);

  wire and_2_out, and_3_out, and_4_out, nA, nQ, nQ_0, nQ_1, nQ_2, or_1_out, or_2_out, or_3_out, Q, Q_0, Q_1,
       Q_2;

  and and_1 (Q, nQ_1, Q_0);
  Seven_Seg_Hex seven_seg_hex_1 (.d({1'b0, Q_2, Q_1, Q_0}), .dp(1'b0));
  not not_1 (nA, A);
  not not_2 (nQ, Q);
  and and_2 (and_2_out, Q, A);
  or or_1 (or_1_out, Q_2, nA);
  or or_2 (or_2_out, and_2_out, nQ_0);
  and and_3 (and_3_out, or_1_out, Q);
  and and_4 (and_4_out, or_2_out, nQ_2);
  or or_3 (or_3_out, nQ, nA);
  D_FF D_2 (.D(and_3_out), .C(clk), .Q(Q_2), .nQ(nQ_2));
  D_FF D_1 (.D(and_4_out), .C(clk), .Q(Q_1), .nQ(nQ_1));
  D_FF D_0 (.D(or_3_out), .C(clk), .Q(Q_0), .nQ(nQ_0));
endmodule
