// Digital circuit lab8.dig as structural Verilog
module lab8 (
  input  clk,
  input  in_2,
  input  in_3,
  input  in_4,
  input  in_5
);

  wire demultiplexer_1_out_0, demultiplexer_1_out_1, demultiplexer_1_out_2, demultiplexer_1_out_3,
       demultiplexer_1_out_4, demultiplexer_1_out_5, demultiplexer_1_out_6, demultiplexer_1_out_7,
       multiplexer_1_out, not_1_out, not_2_out;
  wire [2:0] counterpreset_1_out, d_ff_1_q;

  D_FF d_ff_1 (.D(in_2), .C(in_5), .Q(d_ff_1_q[0]));  // open: nQ
  D_FF d_ff_2 (.D(in_3), .C(in_5), .Q(d_ff_1_q[1]));  // open: nQ
  D_FF d_ff_3 (.D(in_4), .C(in_5), .Q(d_ff_1_q[2]));  // open: nQ
  Multiplexer #(.Selector_Bits(3)) multiplexer_1 (
    .sel(counterpreset_1_out), .in_0(demultiplexer_1_out_0), .in_1(demultiplexer_1_out_1),
    .in_2(demultiplexer_1_out_2), .in_3(demultiplexer_1_out_3), .in_4(demultiplexer_1_out_4),
    .in_5(demultiplexer_1_out_5), .in_6(demultiplexer_1_out_6), .in_7(demultiplexer_1_out_7),
    .out(multiplexer_1_out));
  Demultiplexer #(.Selector_Bits(3)) demultiplexer_1 (
    .sel(d_ff_1_q), .in(1'b1), .out_0(demultiplexer_1_out_0), .out_1(demultiplexer_1_out_1),
    .out_2(demultiplexer_1_out_2), .out_3(demultiplexer_1_out_3), .out_4(demultiplexer_1_out_4),
    .out_5(demultiplexer_1_out_5), .out_6(demultiplexer_1_out_6), .out_7(demultiplexer_1_out_7));
  not not_1 (not_1_out, multiplexer_1_out);
  CounterPreset #(.Bits(3)) counterpreset_1 (
    .en(not_1_out), .C(clk), .dir(1'b0), .in(3'b000), .ld(not_2_out), .clr(1'b0), .out(counterpreset_1_out));  // open: ovf
  not not_2 (not_2_out, in_5);
  Seven_Seg_Hex seven_seg_hex_1 (.d({1'b0, counterpreset_1_out}), .dp(1'b0));
endmodule
